# Fritzing sketch SmartRemoteControlCar (saved by Fritzing 0.9.3b)
breadboards: 1

parts:
  ArduinoUno = Arduino Uno (Rev3)
  H-Bridge_with_L298N = H-Bridge with L298N
  Power_12V = Power plug
  MotorDC = DC Motor
  MotorDC_2 = DC Motor
  LED2 = smd LED [color="Red (633nm)" package="1206 [SMD]"]
  LED3 = smd LED [color="Red (633nm)" package="1206 [SMD]"]
  LED4 = smd LED [color="Red (633nm)" package="1206 [SMD]"]
  Sensor_Ultrasonic_HC-05 = Bluetooth HC-05 Macho
  hc-sr4 = hc-sr04
  LED1 = smd LED [color="Red (633nm)" package="1206 [SMD]"]

nets:
  N1: ArduinoUno.D8, hc-sr4.Trig
  N2: ArduinoUno.D9_PWM, hc-sr4.Echo
  GND: ArduinoUno.GND, LED2.cathode, LED3.cathode, LED4.cathode, Sensor_Ultrasonic_HC-05.GND, hc-sr4.GND, LED1.cathode
  N3: ArduinoUno.D0/RX, Sensor_Ultrasonic_HC-05.TXD
  N4: ArduinoUno.D1/TX, Sensor_Ultrasonic_HC-05.RXD
  N5: ArduinoUno.D2, H-Bridge_with_L298N.IN1
  N6: ArduinoUno.D3_PWM, H-Bridge_with_L298N.IN2
  N7: ArduinoUno.D4, H-Bridge_with_L298N.IN3
  N8: ArduinoUno.D5_PWM, H-Bridge_with_L298N.IN4
  N9: ArduinoUno.D6_PWM, H-Bridge_with_L298N.ENA
  N10: ArduinoUno.D7, LED2.anode, LED3.anode, LED4.anode, LED1.anode
  VCC: ArduinoUno.5V, Sensor_Ultrasonic_HC-05.VCC, hc-sr4.VCC
  12V: H-Bridge_with_L298N.12V, Power_12V.VCC
  GND_2: H-Bridge_with_L298N.GND, Power_12V.GND
  N11: H-Bridge_with_L298N.ENB, H-Bridge_with_L298N.ENB-5V
  N12: H-Bridge_with_L298N.M1-01, MotorDC.pin_2
  N13: H-Bridge_with_L298N.M1-02, MotorDC.pin_1
  N14: H-Bridge_with_L298N.M2-01, MotorDC_2.pin_2
  N15: H-Bridge_with_L298N.M2-02, MotorDC_2.pin_1

custom parts:
  H-Bridge with L298N: h-bridge
